# Fritzing sketch Working with Ultrasonic Sensor (saved by Fritzing 0.9.3b)
breadboards: 1

parts:
  Part1 = Arduino Uno (Rev3)
  LCD1 = LCD screen  # not connected
  LCM1602_IIC1 = LCM1602 IIC [part_number="LCM1602 IIC" chip_label="LCM1602 IIC" package="DIP (Dual Inline) [THT]"]
  U1 = HC-SR04 [chip_label=IC package="SIP (Single Inline) [THT]"]

nets:
  N1: Part1.A4/SDA, LCM1602_IIC1.SDA
  N2: Part1.A5/SCL, LCM1602_IIC1.SCL
  N3: Part1.D2, U1.Echo
  N4: Part1.D3_PWM, U1.Trig
  VCC: Part1.5V, LCM1602_IIC1.VCC, U1.Vcc
  GND: Part1.GND, LCM1602_IIC1.GND, U1.GND
  N5: LCM1602_IIC1.LED_A, LCM1602_IIC1.LED_B

custom parts:
  LCM1602 IIC: I2C-Module to use a 1602 or 2004 LCD on with the wire.h libory Serial LCD Modul
  HC-SR04: HC-SR04 ultrasound distance sensor
